# Fritzing sketch FND_CC (saved by Fritzing 0.9.3b)
breadboards: 1

parts:
  부품1 = Arduino Uno (Rev3)
  R1 = Resistor [tolerance=±5% resistance=220 package=THT]
  R3 = Resistor [tolerance=±5% resistance=220 package=THT]
  R4 = Resistor [tolerance=±5% resistance=220 package=THT]
  R5 = Resistor [tolerance=±5% resistance=220 package=THT]
  R6 = Resistor [tolerance=±5% resistance=220 package=THT]
  R7 = Resistor [tolerance=±5% resistance=220 package=THT]
  R8 = Resistor [tolerance=±5% resistance=220 package=THT]
  R9 = Resistor [tolerance=±5% resistance=220 package=THT]
  U1 = 7-SEGMENT-DISPLAY [package=7-segment-display]

nets:
  N1: 부품1.D8, R6.Pin_0
  N2: 부품1.D9_PWM, R3.Pin_1
  N3: 부품1.GND, U1.C, U1.F
  N4: 부품1.D2, R9.Pin_1
  N5: 부품1.D3_PWM, R1.Pin_1
  N6: 부품1.D4, R4.Pin_1
  N7: 부품1.D5_PWM, R7.Pin_0
  N8: 부품1.D6_PWM, R8.Pin_0
  N9: 부품1.D7, R5.Pin_0
  N10: R1.Pin_0, U1.A
  N11: R3.Pin_0, U1.B
  N12: R4.Pin_0, U1.DP
  N13: R5.Pin_1, U1.G
  N14: R6.Pin_1, U1.E
  N15: R7.Pin_1, U1.G1
  N16: R8.Pin_1, U1.D
  N17: R9.Pin_0, U1.G2
